# Fritzing sketch 10-led (saved by Fritzing 0.9.3b)
breadboards: 1

parts:
  part = Resistor [tolerance=±5% resistance=1k package=THT]
  LED = LED - 5mm [color="Red (633nm)" package="5 mm [THT]"]
  VCC = Battery block 9V
  Switch = Pushbutton [package="[THT]"]

nets:
  N1: part.Pin_0, LED.cathode
  N2: part.Pin_1, VCC.-
  N3: LED.anode, Switch.Pin_1, Switch.Pin_2
  N4: VCC.+, Switch.Pin_3, Switch.Pin_4
