# Fritzing sketch 20-quiz1 (saved by Fritzing 0.9.3b)
breadboards: 1

parts:
  part = Resistor [tolerance=±5% resistance=680k package=THT]
  VCC = Battery block 9V
  Switch = Pushbutton [package="[THT]"]

nets:
  N1: part.Pin_0, Switch.Pin_1, Switch.Pin_2
  GND: part.Pin_1, VCC.-
  N2: VCC.+, Switch.Pin_3, Switch.Pin_4
